// Logisim project circuito-logisim.circ as structural Verilog: 7 circuits, main circuit main
module main (
  input  _5,
  input  _4,
  input  _3,
  input  _2,
  input  _1,
  input  _0,
  input  _5_2,
  input  _4_2,
  input  _3_2,
  input  _2_2,
  input  _1_2,
  input  _0_2,
  input  _5_3,
  input  _4_3,
  input  _3_3,
  input  _2_3,
  input  _1_3,
  input  _0_3,
  input  _5_4,
  input  _4_4,
  input  _3_4,
  input  _2_4,
  input  _1_4,
  input  _0_4,
  input  _5_5,
  input  _4_5,
  input  _3_5,
  input  _2_5,
  input  _1_5,
  input  _0_5,
  input  _5_6,
  input  _4_6,
  input  _3_6,
  input  _2_6,
  input  _1_6,
  input  _0_6
);

  wire bcd_1_s0, bcd_1_s1, bcd_1_s2, bcd_1_s3, bcd_1_s4, bcd_1_s5, bcd_1_s6, bcd_1_s7, bcd_2_s0, bcd_2_s1,
       bcd_2_s2, bcd_2_s3, bcd_2_s4, bcd_2_s5, bcd_2_s6, bcd_2_s7, comparador_1_a___b, comparador_1_a___b_2,
       comparador_1_a_b, decoder_1_a, decoder_1_b, decoder_1_c, decoder_1_d, decoder_1_e, decoder_1_f,
       decoder_1_g, decoder_2_a, decoder_2_b, decoder_2_c, decoder_2_d, decoder_2_e, decoder_2_f,
       decoder_2_g, decoder_3_a, decoder_3_b, decoder_3_c, decoder_3_d, decoder_3_e, decoder_3_f,
       decoder_3_g, decoder_4_a, decoder_4_b, decoder_4_c, decoder_4_d, decoder_4_e, decoder_4_f,
       decoder_4_g, jugador_1_2_s0, jugador_1_2_s1, jugador_1_2_s2, jugador_1_2_s3, jugador_1_3_s0,
       jugador_1_3_s1, jugador_1_3_s2, jugador_1_cout, jugador_1_s0, jugador_1_s1, jugador_1_s2,
       jugador_2_2_s0, jugador_2_2_s1, jugador_2_2_s2, jugador_2_3_cout, jugador_2_3_s0, jugador_2_3_s1,
       jugador_2_3_s2, jugador_2_4_s0, jugador_2_4_s1, jugador_2_4_s2, jugador_2_4_s3, jugador_2_5_s0,
       jugador_2_5_s1, jugador_2_5_s2, jugador_2_s0, jugador_2_s1, jugador_2_s2, jugador__1_2_s0,
       jugador__1_2_s1, jugador__1_2_s2, jugador__1_s0, jugador__1_s1, jugador__1_s2;

  codificador jugador__1 (
    .A0(_5), .A1(_4), .A2(_3), .A3(_2), .A4(_1), .A5(_0), .S0(jugador__1_s0), .S1(jugador__1_s1),
    .S2(jugador__1_s2));
  codificador jugador_2 (
    .A0(_5_3), .A1(_4_3), .A2(_3_3), .A3(_2_3), .A4(_1_3), .A5(_0_3), .S0(jugador_2_s0), .S1(jugador_2_s1),
    .S2(jugador_2_s2));
  codificador jugador__1_2 (
    .A0(_5_4), .A1(_4_4), .A2(_3_4), .A3(_2_4), .A4(_1_4), .A5(_0_4), .S0(jugador__1_2_s0),
    .S1(jugador__1_2_s1), .S2(jugador__1_2_s2));
  codificador jugador_2_2 (
    .A0(_5_5), .A1(_4_5), .A2(_3_5), .A3(_2_5), .A4(_1_5), .A5(_0_5), .S0(jugador_2_2_s0),
    .S1(jugador_2_2_s1), .S2(jugador_2_2_s2));
  LED MSB (.in(jugador__1_s0));
  LED led_1 (.in(jugador__1_s1));
  LED led_2 (.in(jugador_2_s1));
  LED MSB_2 (.in(jugador_2_s0));
  LED MSB_3 (.in(jugador__1_2_s0));
  LED led_3 (.in(jugador__1_2_s1));
  LED led_4 (.in(jugador_2_2_s1));
  LED MSB_4 (.in(jugador_2_2_s0));
  LED LSB (.in(jugador__1_s2));
  LED LSB_2 (.in(jugador_2_s2));
  LED LSB_3 (.in(jugador__1_2_s2));
  LED LSB_4 (.in(jugador_2_2_s2));
  sumador_3_bits jugador_1 (
    .A(jugador__1_s2), .C(jugador__1_s1), .E(jugador__1_s0), .B(jugador__1_2_s2), .D(jugador__1_2_s1),
    .F(jugador__1_2_s0), .CIN(1'b0), .COUT(jugador_1_cout), .S0(jugador_1_s0), .S1(jugador_1_s1),
    .S2(jugador_1_s2));
  sumador_3_bits jugador_2_3 (
    .A(jugador_2_s2), .C(jugador_2_s1), .E(jugador_2_s0), .B(jugador_2_2_s2), .D(jugador_2_2_s1),
    .F(jugador_2_2_s0), .CIN(1'b0), .COUT(jugador_2_3_cout), .S0(jugador_2_3_s0), .S1(jugador_2_3_s1),
    .S2(jugador_2_3_s2));
  sumador_4_bits jugador_1_2 (
    .A(jugador_1_s0), .C(jugador_1_s1), .E(jugador_1_s2), .G(jugador_1_cout), .B(jugador_1_3_s2),
    .D(jugador_1_3_s1), .F(jugador_1_3_s0), .H(1'b0), .CIN(1'b0), .S0(jugador_1_2_s0), .S1(jugador_1_2_s1),
    .S2(jugador_1_2_s2), .S3(jugador_1_2_s3));  // open: COUT
  LED led_5 (.in(jugador_1_2_s2));
  LED MSB_5 (.in(jugador_1_2_s3));
  LED led_6 (.in(jugador_1_2_s1));
  LED led_7 (.in(jugador_2_4_s2));
  LED MSB_6 (.in(jugador_2_4_s3));
  LED led_8 (.in(jugador_2_4_s1));
  sumador_4_bits jugador_2_4 (
    .A(jugador_2_3_s0), .C(jugador_2_3_s1), .E(jugador_2_3_s2), .G(jugador_2_3_cout), .B(jugador_2_5_s2),
    .D(jugador_2_5_s1), .F(jugador_2_5_s0), .H(1'b0), .CIN(1'b0), .S0(jugador_2_4_s0), .S1(jugador_2_4_s1),
    .S2(jugador_2_4_s2), .S3(jugador_2_4_s3));  // open: COUT
  LED LSB_5 (.in(jugador_1_2_s0));
  LED MSB_7 (.in(jugador_1_3_s0));
  LED LSB_6 (.in(jugador_2_4_s0));
  LED led_9 (.in(jugador_1_3_s1));
  LED LSB_7 (.in(jugador_1_3_s2));
  codificador jugador_1_3 (
    .A0(_5_2), .A1(_4_2), .A2(_3_2), .A3(_2_2), .A4(_1_2), .A5(_0_2), .S0(jugador_1_3_s0),
    .S1(jugador_1_3_s1), .S2(jugador_1_3_s2));
  LED led_10 (.in(jugador_2_5_s1));
  LED LSB_8 (.in(jugador_2_5_s2));
  LED MSB_8 (.in(jugador_2_5_s0));
  codificador jugador_2_5 (
    .A0(_5_6), .A1(_4_6), .A2(_3_6), .A3(_2_6), .A4(_1_6), .A5(_0_6), .S0(jugador_2_5_s0),
    .S1(jugador_2_5_s1), .S2(jugador_2_5_s2));
  BCD bcd_1 (
    .B3(jugador_1_2_s3), .B2(jugador_1_2_s2), .B1(jugador_1_2_s1), .B0(jugador_1_2_s0), .S7(bcd_1_s7),
    .S6(bcd_1_s6), .S5(bcd_1_s5), .S4(bcd_1_s4), .S3(bcd_1_s3), .S2(bcd_1_s2), .S1(bcd_1_s1), .S0(bcd_1_s0));
  BCD bcd_2 (
    .B3(jugador_2_4_s3), .B2(jugador_2_4_s2), .B1(jugador_2_4_s1), .B0(jugador_2_4_s0), .S7(bcd_2_s7),
    .S6(bcd_2_s6), .S5(bcd_2_s5), .S4(bcd_2_s4), .S3(bcd_2_s3), .S2(bcd_2_s2), .S1(bcd_2_s1), .S0(bcd_2_s0));
  decoder decoder_1 (
    .B3(bcd_1_s7), .B2(bcd_1_s6), .B1(bcd_1_s5), .B0(bcd_1_s4), .a(decoder_1_a), .b(decoder_1_b),
    .c(decoder_1_c), .d(decoder_1_d), .e(decoder_1_e), .f(decoder_1_f), .g(decoder_1_g));
  decoder decoder_2 (
    .B3(bcd_1_s3), .B2(bcd_1_s2), .B1(bcd_1_s1), .B0(bcd_1_s0), .a(decoder_2_a), .b(decoder_2_b),
    .c(decoder_2_c), .d(decoder_2_d), .e(decoder_2_e), .f(decoder_2_f), .g(decoder_2_g));
  LED jugador_1_4 (.in(comparador_1_a___b));
  comparador comparador_1 (
    .A1(jugador_1_2_s1), .A3(jugador_1_2_s2), .A0(jugador_1_2_s0), .A2(jugador_1_2_s3), .B1(jugador_2_4_s1),
    .B3(jugador_2_4_s2), .B0(jugador_2_4_s0), .B2(jugador_2_4_s3), .A_B(comparador_1_a_b),
    .A___B(comparador_1_a___b), .A___B_2(comparador_1_a___b_2));
  decoder decoder_3 (
    .B3(bcd_2_s7), .B2(bcd_2_s6), .B1(bcd_2_s5), .B0(bcd_2_s4), .a(decoder_3_a), .b(decoder_3_b),
    .c(decoder_3_c), .d(decoder_3_d), .e(decoder_3_e), .f(decoder_3_f), .g(decoder_3_g));
  decoder decoder_4 (
    .B3(bcd_2_s3), .B2(bcd_2_s2), .B1(bcd_2_s1), .B0(bcd_2_s0), .a(decoder_4_a), .b(decoder_4_b),
    .c(decoder_4_c), .d(decoder_4_d), .e(decoder_4_e), .f(decoder_4_f), .g(decoder_4_g));
  _7_Segment_Display u_7_segment_display_1 (
    .g(decoder_1_g), .f(decoder_1_f), .a(decoder_1_a), .b(decoder_1_b), .e(decoder_1_e), .d(decoder_1_d),
    .c(decoder_1_c));  // open: dp
  _7_Segment_Display u_7_segment_display_2 (
    .g(decoder_2_g), .f(decoder_2_f), .a(decoder_2_a), .b(decoder_2_b), .e(decoder_2_e), .d(decoder_2_d),
    .c(decoder_2_c));  // open: dp
  _7_Segment_Display u_7_segment_display_3 (
    .g(decoder_3_g), .f(decoder_3_f), .a(decoder_3_a), .b(decoder_3_b), .e(decoder_3_e), .d(decoder_3_d),
    .c(decoder_3_c));  // open: dp
  _7_Segment_Display u_7_segment_display_4 (
    .g(decoder_4_g), .f(decoder_4_f), .a(decoder_4_a), .b(decoder_4_b), .e(decoder_4_e), .d(decoder_4_d),
    .c(decoder_4_c));  // open: dp
  LED jugador_2_6 (.in(comparador_1_a___b_2));
  LED empate (.in(comparador_1_a_b));

  // Notes on the sheet:
  //   juez 1
  //   juez 2
  //   jugador 1
  //    jugador 2
  //   juez 3
  //   juez 3
  //   puntuación jugador 1
  //   decenas
  //   unidades
  //   puntuación jugador 2
  //   decenas
  //   unidades
endmodule

module codificador (
  input  A0,
  input  A1,
  input  A2,
  input  A3,
  input  A4,
  input  A5,
  output S0,
  output S1,
  output S2
);

  or or_1 (S0, A0, A1);
  or or_2 (S1, A2, A3);
  or or_3 (S2, A0, A2, A4);

  // Notes on the sheet:
  //   MSB
  //   LSB
endmodule

// sumador
module sumador_3_bits (
  input  A,
  input  C,
  input  E,
  input  B,
  input  D,
  input  F,
  input  CIN,
  output COUT,
  output S0,
  output S1,
  output S2
);

  wire and_1_out, and_2_out, and_3_out, and_4_out, and_5_out, and_6_out, and_7_out, and_8_out, and_9_out,
       and_10_out, and_11_out, and_12_out, and_13_out, and_14_out, and_15_out, and_16_out, and_17_out,
       and_18_out, and_19_out, and_20_out, and_21_out, not_1_out, not_2_out, not_3_out, not_4_out, not_5_out,
       not_6_out, not_7_out, not_8_out, not_9_out, not_10_out, not_11_out, not_12_out, not_13_out,
       not_14_out, not_15_out, not_16_out, not_17_out, not_18_out, or_1_out, or_3_out;

  and and_1 (and_1_out, A, CIN);
  and and_2 (and_2_out, B, CIN);
  and and_3 (and_3_out, A, B);
  not not_1 (not_1_out, B);
  not not_2 (not_2_out, CIN);
  not not_3 (not_3_out, A);
  not not_4 (not_4_out, B);
  not not_5 (not_5_out, A);
  not not_6 (not_6_out, CIN);
  or or_1 (or_1_out, and_1_out, and_2_out, and_3_out);
  and and_4 (and_4_out, A, not_1_out, not_2_out);
  and and_5 (and_5_out, not_3_out, not_4_out, CIN);
  and and_6 (and_6_out, A, B, CIN);
  and and_7 (and_7_out, not_5_out, B, not_6_out);
  or or_2 (S0, and_4_out, and_5_out, and_6_out, and_7_out);
  and and_8 (and_8_out, C, or_1_out);
  and and_9 (and_9_out, D, or_1_out);
  and and_10 (and_10_out, C, D);
  not not_7 (not_7_out, D);
  not not_8 (not_8_out, or_1_out);
  not not_9 (not_9_out, C);
  not not_10 (not_10_out, D);
  not not_11 (not_11_out, C);
  not not_12 (not_12_out, or_1_out);
  or or_3 (or_3_out, and_8_out, and_9_out, and_10_out);
  and and_11 (and_11_out, C, not_7_out, not_8_out);
  and and_12 (and_12_out, not_9_out, not_10_out, or_1_out);
  and and_13 (and_13_out, C, D, or_1_out);
  and and_14 (and_14_out, not_11_out, D, not_12_out);
  or or_4 (S1, and_11_out, and_12_out, and_13_out, and_14_out);
  and and_15 (and_15_out, E, or_3_out);
  and and_16 (and_16_out, F, or_3_out);
  and and_17 (and_17_out, E, F);
  not not_13 (not_13_out, F);
  and and_18 (and_18_out, E, not_13_out, not_14_out);
  not not_14 (not_14_out, or_3_out);
  not not_15 (not_15_out, E);
  and and_19 (and_19_out, not_15_out, not_16_out, or_3_out);
  not not_16 (not_16_out, F);
  and and_20 (and_20_out, E, F, or_3_out);
  not not_17 (not_17_out, E);
  and and_21 (and_21_out, not_17_out, F, not_18_out);
  not not_18 (not_18_out, or_3_out);
  or or_5 (COUT, and_15_out, and_16_out, and_17_out);
  or or_6 (S2, and_18_out, and_19_out, and_20_out, and_21_out);

  // Notes on the sheet:
  //   LSB
  //   COUT
  //   COUT
  //   MSB
endmodule

// sumador
module sumador_4_bits (
  input  A,
  input  C,
  input  E,
  input  G,
  input  B,
  input  D,
  input  F,
  input  H,
  input  CIN,
  output COUT,
  output S0,
  output S1,
  output S2,
  output S3
);

  wire and_1_out, and_2_out, and_3_out, and_4_out, and_5_out, and_6_out, and_7_out, and_8_out, and_9_out,
       and_10_out, and_11_out, and_12_out, and_13_out, and_14_out, and_15_out, and_16_out, and_17_out,
       and_18_out, and_19_out, and_20_out, and_21_out, and_22_out, and_23_out, and_24_out, and_25_out,
       and_26_out, and_27_out, and_28_out, not_1_out, not_2_out, not_3_out, not_4_out, not_5_out, not_6_out,
       not_7_out, not_8_out, not_9_out, not_10_out, not_11_out, not_12_out, not_13_out, not_14_out,
       not_15_out, not_16_out, not_17_out, not_18_out, not_19_out, not_20_out, not_21_out, not_22_out,
       not_23_out, not_24_out, or_1_out, or_3_out, or_5_out;

  and and_1 (and_1_out, A, CIN);
  and and_2 (and_2_out, B, CIN);
  and and_3 (and_3_out, A, B);
  not not_1 (not_1_out, B);
  not not_2 (not_2_out, CIN);
  not not_3 (not_3_out, A);
  not not_4 (not_4_out, B);
  not not_5 (not_5_out, A);
  not not_6 (not_6_out, CIN);
  or or_1 (or_1_out, and_1_out, and_2_out, and_3_out);
  and and_4 (and_4_out, A, not_1_out, not_2_out);
  and and_5 (and_5_out, not_3_out, not_4_out, CIN);
  and and_6 (and_6_out, A, B, CIN);
  and and_7 (and_7_out, not_5_out, B, not_6_out);
  or or_2 (S0, and_4_out, and_5_out, and_6_out, and_7_out);
  and and_8 (and_8_out, C, or_1_out);
  and and_9 (and_9_out, D, or_1_out);
  and and_10 (and_10_out, C, D);
  not not_7 (not_7_out, D);
  not not_8 (not_8_out, or_1_out);
  not not_9 (not_9_out, C);
  not not_10 (not_10_out, D);
  not not_11 (not_11_out, C);
  not not_12 (not_12_out, or_1_out);
  or or_3 (or_3_out, and_8_out, and_9_out, and_10_out);
  and and_11 (and_11_out, C, not_7_out, not_8_out);
  and and_12 (and_12_out, not_9_out, not_10_out, or_1_out);
  and and_13 (and_13_out, C, D, or_1_out);
  and and_14 (and_14_out, not_11_out, D, not_12_out);
  or or_4 (S1, and_11_out, and_12_out, and_13_out, and_14_out);
  and and_15 (and_15_out, E, or_3_out);
  and and_16 (and_16_out, F, or_3_out);
  and and_17 (and_17_out, E, F);
  not not_13 (not_13_out, F);
  and and_18 (and_18_out, E, not_13_out, not_14_out);
  not not_14 (not_14_out, or_3_out);
  not not_15 (not_15_out, E);
  not not_16 (not_16_out, F);
  and and_19 (and_19_out, not_15_out, not_16_out, or_3_out);
  and and_20 (and_20_out, E, F, or_3_out);
  not not_17 (not_17_out, E);
  and and_21 (and_21_out, not_17_out, F, not_18_out);
  not not_18 (not_18_out, or_3_out);
  or or_5 (or_5_out, and_15_out, and_16_out, and_17_out);
  or or_6 (S2, and_18_out, and_19_out, and_20_out, and_21_out);
  and and_22 (and_22_out, G, or_5_out);
  and and_23 (and_23_out, H, or_5_out);
  and and_24 (and_24_out, G, H);
  not not_19 (not_19_out, H);
  not not_20 (not_20_out, or_5_out);
  not not_21 (not_21_out, G);
  not not_22 (not_22_out, H);
  not not_23 (not_23_out, G);
  not not_24 (not_24_out, or_5_out);
  or or_7 (COUT, and_22_out, and_23_out, and_24_out);
  and and_25 (and_25_out, G, not_19_out, not_20_out);
  and and_26 (and_26_out, not_21_out, not_22_out, or_5_out);
  and and_27 (and_27_out, G, H, or_5_out);
  and and_28 (and_28_out, not_23_out, H, not_24_out);
  or or_8 (S3, and_25_out, and_26_out, and_27_out, and_28_out);

  // Notes on the sheet:
  //   LSB
  //   COUT
  //   COUT
  //   MSB
endmodule

module decoder (
  input  B3,
  input  B2,
  input  B1,
  input  B0,
  output a,
  output b,
  output c,
  output d,
  output e,
  output f,
  output g
);

  wire and_1_out, and_2_out, and_3_out, and_4_out, and_5_out, and_6_out, and_7_out, and_8_out, and_9_out,
       and_10_out, and_11_out, and_12_out, and_13_out, and_14_out, and_15_out, and_16_out, not_1_out,
       not_2_out, not_3_out, not_4_out, not_5_out, not_6_out, not_7_out, not_8_out, not_9_out, not_10_out,
       not_11_out, not_12_out, not_13_out, not_14_out, not_15_out, not_16_out, not_17_out, not_18_out,
       not_19_out, not_20_out, not_21_out;

  not not_1 (not_1_out, B2);
  and and_1 (and_1_out, not_1_out, not_2_out);
  not not_2 (not_2_out, B0);
  and and_2 (and_2_out, B2, B0);
  not not_3 (not_3_out, B2);
  not not_4 (not_4_out, B1);
  and and_3 (and_3_out, not_4_out, not_5_out);
  not not_5 (not_5_out, B0);
  and and_4 (and_4_out, B1, B0);
  not not_6 (not_6_out, B1);
  or or_1 (c, not_6_out, B0, B2);
  not not_7 (not_7_out, B2);
  and and_5 (and_5_out, not_7_out, not_8_out);
  not not_8 (not_8_out, B0);
  not not_9 (not_9_out, B2);
  and and_6 (and_6_out, not_9_out, B1);
  and and_7 (and_7_out, B1, not_10_out);
  not not_10 (not_10_out, B0);
  not not_11 (not_11_out, B1);
  and and_8 (and_8_out, B2, not_11_out, B0);
  not not_12 (not_12_out, B2);
  and and_9 (and_9_out, not_12_out, not_13_out);
  not not_13 (not_13_out, B0);
  and and_10 (and_10_out, B1, not_14_out);
  not not_14 (not_14_out, B0);
  not not_15 (not_15_out, B1);
  and and_11 (and_11_out, not_15_out, not_16_out);
  not not_16 (not_16_out, B0);
  and and_12 (and_12_out, B2, not_17_out);
  not not_17 (not_17_out, B1);
  and and_13 (and_13_out, B2, not_18_out);
  not not_18 (not_18_out, B0);
  not not_19 (not_19_out, B2);
  and and_14 (and_14_out, not_19_out, B1);
  and and_15 (and_15_out, B2, not_20_out);
  not not_20 (not_20_out, B1);
  and and_16 (and_16_out, B2, not_21_out);
  not not_21 (not_21_out, B0);
  or or_2 (a, and_1_out, B1, and_2_out, B3);
  or or_3 (b, not_3_out, and_3_out, and_4_out);
  or or_4 (d, and_5_out, and_6_out, and_7_out, and_8_out);
  or or_5 (e, and_9_out, and_10_out);
  or or_6 (f, and_11_out, and_12_out, and_13_out, B3);
  or or_7 (g, and_14_out, and_15_out, and_16_out, B3);

  // Notes on the sheet:
  //   decoder de 4 bits a display de 7 segmentos
endmodule

module BCD (
  input  B3,
  input  B2,
  input  B1,
  input  B0,
  output S7,
  output S6,
  output S5,
  output S4,
  output S3,
  output S2,
  output S1,
  output S0
);

  wire and_1_out, and_2_out, and_4_out, and_5_out, and_6_out, and_7_out, not_1_out, not_2_out, not_3_out,
       not_4_out, not_5_out;

  and and_1 (and_1_out, B3, B2);
  and and_2 (and_2_out, B3, B1);
  and and_3 (S3, B3, not_1_out, not_2_out);
  not not_1 (not_1_out, B2);
  not not_2 (not_2_out, B1);
  not not_3 (not_3_out, B3);
  and and_4 (and_4_out, not_3_out, B2);
  and and_5 (and_5_out, B2, B1);
  and and_6 (and_6_out, B3, B2, not_4_out);
  not not_4 (not_4_out, B1);
  not not_5 (not_5_out, B3);
  and and_7 (and_7_out, not_5_out, B1);
  not not_6 (S7, 1'b1);
  not not_7 (S6, 1'b1);
  not not_8 (S5, 1'b1);
  or or_1 (S4, and_1_out, and_2_out);
  or or_2 (S2, and_4_out, and_5_out);
  or or_3 (S1, and_6_out, and_7_out);

  assign S0 = B0;

  // Notes on the sheet:
  //   BCD de 4 bits a 8 bits
  //   Decenas: S7 S6 S5 S4
  //   Unidades: S3 S2 S1 S0
endmodule

module comparador (
  input  A1,
  input  A3,
  input  A0,
  input  A2,
  input  B1,
  input  B3,
  input  B0,
  input  B2,
  output A___B,
  output A___B_2,
  output A_B
);

  wire and_2_out, and_3_out, and_4_out, and_5_out, and_6_out, and_7_out, and_8_out, and_9_out, and_10_out,
       and_11_out, and_12_out, and_13_out, and_14_out, and_15_out, and_16_out, and_17_out, and_18_out,
       and_19_out, and_20_out, and_21_out, not_1_out, not_2_out, not_3_out, not_4_out, not_5_out, not_6_out,
       not_7_out, not_8_out, not_9_out, not_10_out, not_11_out, not_12_out, not_13_out, not_14_out,
       not_15_out, not_16_out, not_17_out, not_18_out, not_19_out, not_20_out, not_21_out, not_22_out,
       not_23_out, not_24_out, or_1_out, or_2_out, or_3_out, or_4_out, xnor_1_out, xnor_2_out, xnor_3_out,
       xnor_4_out, xnor_5_out, xnor_6_out;

  not not_1 (not_1_out, B1);
  not not_2 (not_2_out, B1);
  not not_3 (not_3_out, B0);
  not not_4 (not_4_out, B0);
  not not_5 (not_5_out, A1);
  not not_6 (not_6_out, A0);
  not not_7 (not_7_out, A1);
  not not_8 (not_8_out, A0);
  xnor xnor_1 (xnor_1_out, A1, B1);
  xnor xnor_2 (xnor_2_out, A0, B0);
  and and_1 (A_B, and_8_out, and_15_out);
  and and_2 (and_2_out, A1, not_1_out);
  and and_3 (and_3_out, A0, not_2_out, not_3_out);
  and and_4 (and_4_out, A1, A0, not_4_out);
  and and_5 (and_5_out, not_5_out, B1);
  and and_6 (and_6_out, not_6_out, B1, B0);
  and and_7 (and_7_out, not_7_out, not_8_out, B0);
  and and_8 (and_8_out, xnor_1_out, xnor_2_out);
  or or_1 (or_1_out, and_2_out, and_3_out, and_4_out);
  or or_2 (or_2_out, and_5_out, and_6_out, and_7_out);
  not not_9 (not_9_out, B3);
  not not_10 (not_10_out, B3);
  not not_11 (not_11_out, B2);
  not not_12 (not_12_out, B2);
  not not_13 (not_13_out, A3);
  not not_14 (not_14_out, A2);
  not not_15 (not_15_out, A3);
  not not_16 (not_16_out, A2);
  xnor xnor_3 (xnor_3_out, A3, B3);
  xnor xnor_4 (xnor_4_out, A2, B2);
  and and_9 (and_9_out, A3, not_9_out);
  and and_10 (and_10_out, A2, not_10_out, not_11_out);
  and and_11 (and_11_out, A3, A2, not_12_out);
  and and_12 (and_12_out, not_13_out, B3);
  and and_13 (and_13_out, not_14_out, B3, B2);
  and and_14 (and_14_out, not_15_out, not_16_out, B2);
  and and_15 (and_15_out, xnor_3_out, xnor_4_out);
  or or_3 (or_3_out, and_9_out, and_10_out, and_11_out);
  or or_4 (or_4_out, and_12_out, and_13_out, and_14_out);
  not not_17 (not_17_out, or_4_out);
  not not_18 (not_18_out, or_4_out);
  not not_19 (not_19_out, or_2_out);
  not not_20 (not_20_out, or_2_out);
  not not_21 (not_21_out, or_3_out);
  not not_22 (not_22_out, or_1_out);
  not not_23 (not_23_out, or_3_out);
  not not_24 (not_24_out, or_1_out);
  and and_16 (and_16_out, or_3_out, not_17_out);
  and and_17 (and_17_out, or_1_out, not_18_out, not_19_out);
  and and_18 (and_18_out, or_3_out, or_1_out, not_20_out);
  and and_19 (and_19_out, not_21_out, or_4_out);
  and and_20 (and_20_out, not_22_out, or_4_out, or_2_out);
  and and_21 (and_21_out, not_23_out, not_24_out, or_2_out);
  xnor xnor_5 (xnor_5_out, or_3_out, or_4_out);
  xnor xnor_6 (xnor_6_out, or_1_out, or_2_out);
  or or_5 (A___B, and_16_out, and_17_out, and_18_out);
  or or_6 (A___B_2, and_19_out, and_20_out, and_21_out);
  // AND_Gate and_22 has open pins: in0=xnor_5_out, in1=xnor_6_out, out=open

  // Notes on the sheet:
  //   LSB
  //   LSB
  //   A1A0 = B1B0
  //   A1A0 > B1B0
  //   A1A0 < B1B0
  //   MSB
  //   MSB
  //   A3A2 = B3B2
  //   A3A2 > B3B2
  //   A3A2 < B3B2
  //   A3A2 > B3B2
  //   A1A0 > B1B0
  //   A3A2 < B3B2
  //   A1A0 < B1B0
endmodule
