// Logisim project circuito-logisim.circ as structural Verilog: 14 circuits, main circuit main
module main (
);

  wire bcd_1_s0, bcd_1_s1, bcd_1_s2, bcd_1_s3, bcd_1_s4, bcd_1_s5, bcd_1_s6, bcd_1_s7, bcd_2_s0, bcd_2_s1,
       bcd_2_s2, bcd_2_s3, bcd_3_s0, bcd_3_s1, bcd_3_s2, bcd_3_s3, bcd_3_s4, bcd_3_s5, bcd_3_s6, bcd_3_s7,
       clock_1_out, contador_amarillo_ff0, contador_amarillo_ff1, contador_rojo_s0, contador_rojo_s1,
       contador_rojo_s2, contador_rojo_s3, contador_rojo_s4, contador_verde_s0, contador_verde_s1,
       contador_verde_s2, contador_verde_s3, decoder_1_a, decoder_1_b, decoder_1_c, decoder_1_d, decoder_1_e,
       decoder_1_f, decoder_1_g, decoder_2_a, decoder_2_b, decoder_2_c, decoder_2_d, decoder_2_e,
       decoder_2_f, decoder_2_g, decoder_3_a, decoder_3_b, decoder_3_c, decoder_3_d, decoder_3_e,
       decoder_3_f, decoder_3_g, decoder_4_a, decoder_4_b, decoder_4_c, decoder_4_d, decoder_4_e,
       decoder_4_f, decoder_4_g, decoder_5_a, decoder_5_b, decoder_5_c, decoder_5_d, decoder_5_e,
       decoder_5_f, decoder_5_g, FF0_2_q, FF0_3_q, FF0_q, FF1_2_q, FF1_3_q, FF1_q, FF2_2_q, FF2_q, FF3_2_q,
       FF3_q, FF4_q, START_out, switch_1_s0, switch_1_s1, switch_1_s2;

  LED Q2 (.in(FF2_q));
  LED Q3 (.in(FF3_q));
  Clock clock_1 (.out(clock_1_out));
  Button START (.out(START_out));
  LED Q0 (.in(FF0_q));
  LED Q1 (.in(FF1_q));
  D_Flip_Flop FF3 (
    .clk(clock_1_out), .D(contador_verde_s3), .Q(FF3_q), .preset(START_out), .en(switch_1_s0), .reset(1'b0));  // open: Qn
  D_Flip_Flop FF2 (
    .clk(clock_1_out), .D(contador_verde_s2), .Q(FF2_q), .preset(START_out), .en(switch_1_s0), .reset(1'b0));  // open: Qn
  _7_Segment_Display u_7_segment_display_1 (
    .g(decoder_1_g), .f(decoder_1_f), .a(decoder_1_a), .b(decoder_1_b), .e(decoder_1_e), .d(decoder_1_d),
    .c(decoder_1_c));  // open: dp
  decoder decoder_1 (
    .B3(bcd_1_s7), .B2(bcd_1_s6), .B1(bcd_1_s5), .B0(bcd_1_s4), .a(decoder_1_a), .b(decoder_1_b),
    .c(decoder_1_c), .d(decoder_1_d), .e(decoder_1_e), .f(decoder_1_f), .g(decoder_1_g));
  bcd bcd_1 (
    .B4(1'b0), .B3(FF3_q), .B2(FF2_q), .B1(FF1_q), .B0(FF0_q), .S7(bcd_1_s7), .S6(bcd_1_s6), .S5(bcd_1_s5),
    .S4(bcd_1_s4), .S3(bcd_1_s3), .S2(bcd_1_s2), .S1(bcd_1_s1), .S0(bcd_1_s0));
  _7_Segment_Display u_7_segment_display_2 (
    .g(decoder_2_g), .f(decoder_2_f), .a(decoder_2_a), .b(decoder_2_b), .e(decoder_2_e), .d(decoder_2_d),
    .c(decoder_2_c));  // open: dp
  decoder decoder_2 (
    .B3(bcd_1_s3), .B2(bcd_1_s2), .B1(bcd_1_s1), .B0(bcd_1_s0), .a(decoder_2_a), .b(decoder_2_b),
    .c(decoder_2_c), .d(decoder_2_d), .e(decoder_2_e), .f(decoder_2_f), .g(decoder_2_g));
  D_Flip_Flop FF1 (
    .clk(clock_1_out), .D(contador_verde_s1), .Q(FF1_q), .preset(1'b0), .en(switch_1_s0), .reset(1'b0));  // open: Qn
  contador_verde contador_verde (
    .Q3(FF3_q), .Q2(FF2_q), .Q1(FF1_q), .Q0(FF0_q), .S3(contador_verde_s3), .S2(contador_verde_s2),
    .S1(contador_verde_s1), .S0(contador_verde_s0));
  D_Flip_Flop FF0 (
    .clk(clock_1_out), .D(contador_verde_s0), .Q(FF0_q), .preset(1'b0), .en(switch_1_s0), .reset(1'b0));  // open: Qn
  switch switch_1 (
    .A3(FF3_q), .A2(FF2_q), .A1(FF1_q), .A0(FF0_q), .B4(FF4_q), .B0(FF0_3_q), .B1(FF1_3_q), .B2(FF2_2_q),
    .B3(FF3_2_q), .S2(switch_1_s2), .S0(switch_1_s0), .S1(switch_1_s1));
  LED verde_activo (.in(switch_1_s0));
  LED rojo_activo (.in(switch_1_s1));
  LED amarillo__activo (.in(switch_1_s2));
  LED Q4 (.in(FF4_q));
  LED led_1 (.in(FF1_2_q));
  LED Q0_2 (.in(FF0_3_q));
  LED Q1_2 (.in(FF1_3_q));
  LED Q2_2 (.in(FF2_2_q));
  LED Q3_2 (.in(FF3_2_q));
  D_Flip_Flop FF4 (
    .clk(clock_1_out), .D(contador_rojo_s4), .Q(FF4_q), .preset(START_out), .en(switch_1_s1), .reset(1'b0));  // open: Qn
  bcd bcd_2 (
    .B4(1'b0), .B3(1'b0), .B2(1'b0), .B1(FF1_2_q), .B0(FF0_2_q), .S3(bcd_2_s3), .S2(bcd_2_s2), .S1(bcd_2_s1),
    .S0(bcd_2_s0));  // open: S7, S6, S5, S4
  LED led_2 (.in(FF0_2_q));
  D_Flip_Flop FF1_2 (
    .clk(clock_1_out), .D(contador_amarillo_ff1), .Q(FF1_2_q), .preset(START_out), .en(switch_1_s2),
    .reset(1'b0));  // open: Qn
  D_Flip_Flop FF0_2 (
    .clk(clock_1_out), .D(contador_amarillo_ff0), .Q(FF0_2_q), .preset(START_out), .en(switch_1_s2),
    .reset(1'b0));  // open: Qn
  _7_Segment_Display u_7_segment_display_3 (
    .g(decoder_3_g), .f(decoder_3_f), .a(decoder_3_a), .b(decoder_3_b), .e(decoder_3_e), .d(decoder_3_d),
    .c(decoder_3_c));  // open: dp
  decoder decoder_3 (
    .B3(bcd_3_s7), .B2(bcd_3_s6), .B1(bcd_3_s5), .B0(bcd_3_s4), .a(decoder_3_a), .b(decoder_3_b),
    .c(decoder_3_c), .d(decoder_3_d), .e(decoder_3_e), .f(decoder_3_f), .g(decoder_3_g));
  bcd bcd_3 (
    .B4(FF4_q), .B3(FF3_2_q), .B2(FF2_2_q), .B1(FF1_3_q), .B0(FF0_3_q), .S7(bcd_3_s7), .S6(bcd_3_s6),
    .S5(bcd_3_s5), .S4(bcd_3_s4), .S3(bcd_3_s3), .S2(bcd_3_s2), .S1(bcd_3_s1), .S0(bcd_3_s0));
  D_Flip_Flop FF3_2 (
    .clk(clock_1_out), .D(contador_rojo_s3), .Q(FF3_2_q), .preset(START_out), .en(switch_1_s1), .reset(1'b0));  // open: Qn
  _7_Segment_Display u_7_segment_display_4 (
    .g(decoder_4_g), .f(decoder_4_f), .a(decoder_4_a), .b(decoder_4_b), .e(decoder_4_e), .d(decoder_4_d),
    .c(decoder_4_c));  // open: dp
  decoder decoder_4 (
    .B3(bcd_2_s3), .B2(bcd_2_s2), .B1(bcd_2_s1), .B0(bcd_2_s0), .a(decoder_4_a), .b(decoder_4_b),
    .c(decoder_4_c), .d(decoder_4_d), .e(decoder_4_e), .f(decoder_4_f), .g(decoder_4_g));
  contador_amarillo contador_amarillo (
    .Q1(FF1_2_q), .Q0(FF0_2_q), .FF1(contador_amarillo_ff1), .FF0(contador_amarillo_ff0));
  _7_Segment_Display u_7_segment_display_5 (
    .g(decoder_5_g), .f(decoder_5_f), .a(decoder_5_a), .b(decoder_5_b), .e(decoder_5_e), .d(decoder_5_d),
    .c(decoder_5_c));  // open: dp
  decoder decoder_5 (
    .B3(bcd_3_s3), .B2(bcd_3_s2), .B1(bcd_3_s1), .B0(bcd_3_s0), .a(decoder_5_a), .b(decoder_5_b),
    .c(decoder_5_c), .d(decoder_5_d), .e(decoder_5_e), .f(decoder_5_f), .g(decoder_5_g));
  D_Flip_Flop FF2_2 (
    .clk(clock_1_out), .D(contador_rojo_s2), .Q(FF2_2_q), .preset(1'b0), .en(switch_1_s1), .reset(1'b0));  // open: Qn
  D_Flip_Flop FF1_3 (
    .clk(clock_1_out), .D(contador_rojo_s1), .Q(FF1_3_q), .preset(1'b0), .en(switch_1_s1), .reset(1'b0));  // open: Qn
  D_Flip_Flop FF0_3 (
    .clk(clock_1_out), .D(contador_rojo_s0), .Q(FF0_3_q), .preset(1'b0), .en(switch_1_s1), .reset(1'b0));  // open: Qn
  contador_rojo contador_rojo (
    .Q4(FF4_q), .Q3(FF3_2_q), .Q2(FF2_2_q), .Q1(FF1_3_q), .Q0(FF0_3_q), .S4(contador_rojo_s4),
    .S3(contador_rojo_s3), .S2(contador_rojo_s2), .S1(contador_rojo_s1), .S0(contador_rojo_s0));

  // Notes on the sheet:
  //   Pasos a seguir:
  //   a) click en el boton START
  //   b) activar el reloj (CTRL+K)
  //   VERDE
  //   AMARILLO
  //   ROJO
endmodule

module contador_verde (
  input  Q3,
  input  Q2,
  input  Q1,
  input  Q0,
  output S3,
  output S2,
  output S1,
  output S0
);

  wire and_1_out, and_2_out, and_3_out, and_4_out, and_5_out, and_6_out, and_7_out, and_8_out, and_9_out,
       and_10_out, and_11_out, and_12_out, and_13_out, and_14_out, not_1_out, not_2_out, not_3_out,
       not_4_out, not_5_out, not_6_out, not_7_out, not_8_out, not_9_out, not_10_out, not_11_out, not_12_out,
       not_13_out, not_14_out, not_15_out, not_16_out, not_17_out, not_18_out, not_19_out, not_20_out,
       not_21_out, not_22_out, not_23_out, not_24_out, not_25_out;

  not not_1 (not_1_out, Q1);
  not not_2 (not_2_out, Q0);
  not not_3 (not_3_out, Q2);
  not not_4 (not_4_out, Q2);
  not not_5 (not_5_out, Q3);
  not not_6 (not_6_out, Q2);
  not not_7 (not_7_out, Q1);
  not not_8 (not_8_out, Q0);
  not not_9 (not_9_out, Q2);
  not not_10 (not_10_out, Q1);
  and and_1 (and_1_out, not_9_out, not_10_out, not_11_out);
  not not_11 (not_11_out, Q0);
  not not_12 (not_12_out, Q3);
  and and_2 (and_2_out, not_12_out, Q2, Q0);
  not not_13 (not_13_out, Q3);
  and and_3 (and_3_out, not_13_out, Q2, Q1);
  and and_4 (and_4_out, Q2, not_14_out, not_15_out);
  not not_14 (not_14_out, Q1);
  not not_15 (not_15_out, Q0);
  and and_5 (and_5_out, Q3, not_16_out, not_17_out);
  not not_16 (not_16_out, Q1);
  not not_17 (not_17_out, Q0);
  not not_18 (not_18_out, Q2);
  and and_6 (and_6_out, not_18_out, Q1, Q0);
  not not_19 (not_19_out, Q3);
  and and_7 (and_7_out, not_19_out, Q1, Q0);
  not not_20 (not_20_out, Q1);
  and and_8 (and_8_out, Q2, not_20_out, not_21_out);
  not not_21 (not_21_out, Q0);
  and and_9 (and_9_out, Q3, not_22_out, not_23_out);
  not not_22 (not_22_out, Q2);
  not not_23 (not_23_out, Q0);
  not not_24 (not_24_out, Q3);
  and and_10 (and_10_out, not_24_out, Q1, not_25_out);
  not not_25 (not_25_out, Q0);
  and and_11 (and_11_out, Q3, Q2, not_1_out, not_2_out);
  and and_12 (and_12_out, Q3, not_3_out, Q0);
  and and_13 (and_13_out, Q3, not_4_out, Q1);
  and and_14 (and_14_out, not_5_out, not_6_out, not_7_out, not_8_out);
  or or_1 (S2, and_1_out, and_2_out, and_3_out);
  or or_2 (S1, and_4_out, and_5_out, and_6_out, and_7_out);
  or or_3 (S0, and_8_out, and_9_out, and_10_out);
  or or_4 (S3, and_11_out, and_12_out, and_13_out, and_14_out);
endmodule

module contador_rojo (
  input  Q4,
  input  Q3,
  input  Q2,
  input  Q1,
  input  Q0,
  output S4,
  output S3,
  output S2,
  output S1,
  output S0
);

  wire and_1_out, and_2_out, and_3_out, and_4_out, and_5_out, and_6_out, and_7_out, and_8_out, and_9_out,
       and_10_out, and_11_out, and_12_out, and_13_out, and_14_out, and_15_out, and_16_out, and_17_out,
       and_18_out, and_19_out, and_20_out, and_21_out, not_1_out, not_2_out, not_3_out, not_4_out, not_5_out,
       not_6_out, not_7_out, not_8_out, not_9_out, not_10_out, not_11_out, not_12_out, not_13_out,
       not_14_out, not_15_out, not_16_out, not_17_out, not_18_out, not_19_out, not_20_out, not_21_out,
       not_22_out, not_23_out, not_24_out, not_25_out, not_26_out, not_27_out;

  not not_1 (not_1_out, Q4);
  not not_2 (not_2_out, Q3);
  not not_3 (not_3_out, Q2);
  not not_4 (not_4_out, Q1);
  not not_5 (not_5_out, Q0);
  not not_6 (not_6_out, Q3);
  not not_7 (not_7_out, Q2);
  not not_8 (not_8_out, Q1);
  not not_9 (not_9_out, Q0);
  not not_10 (not_10_out, Q2);
  not not_11 (not_11_out, Q1);
  not not_12 (not_12_out, Q0);
  not not_13 (not_13_out, Q2);
  not not_14 (not_14_out, Q1);
  not not_15 (not_15_out, Q0);
  not not_16 (not_16_out, Q1);
  not not_17 (not_17_out, Q0);
  not not_18 (not_18_out, Q1);
  not not_19 (not_19_out, Q0);
  not not_20 (not_20_out, Q1);
  not not_21 (not_21_out, Q0);
  not not_22 (not_22_out, Q0);
  not not_23 (not_23_out, Q0);
  not not_24 (not_24_out, Q4);
  not not_25 (not_25_out, Q0);
  not not_26 (not_26_out, Q2);
  not not_27 (not_27_out, Q0);
  and and_1 (and_1_out, Q4, Q0);
  and and_2 (and_2_out, Q4, Q1);
  and and_3 (and_3_out, Q4, Q2);
  and and_4 (and_4_out, Q4, Q3);
  and and_5 (and_5_out, not_1_out, not_2_out, not_3_out, not_4_out, not_5_out);
  and and_6 (and_6_out, Q3, Q0);
  and and_7 (and_7_out, Q3, Q1);
  and and_8 (and_8_out, Q3, Q2);
  and and_9 (and_9_out, not_6_out, not_7_out, not_8_out, not_9_out);
  and and_10 (and_10_out, Q2, Q0);
  and and_11 (and_11_out, Q2, Q1);
  and and_12 (and_12_out, Q3, not_10_out, not_11_out, not_12_out);
  and and_13 (and_13_out, Q4, not_13_out, not_14_out, not_15_out);
  and and_14 (and_14_out, Q1, Q0);
  and and_15 (and_15_out, Q2, not_16_out, not_17_out);
  and and_16 (and_16_out, Q3, not_18_out, not_19_out);
  and and_17 (and_17_out, Q4, not_20_out, not_21_out);
  and and_18 (and_18_out, Q1, not_22_out);
  and and_19 (and_19_out, Q3, not_23_out);
  and and_20 (and_20_out, not_24_out, Q2, not_25_out);
  and and_21 (and_21_out, Q4, not_26_out, not_27_out);
  or or_1 (S4, and_1_out, and_2_out, and_3_out, and_4_out, and_5_out);
  or or_2 (S3, and_6_out, and_7_out, and_8_out, and_9_out);
  or or_3 (S2, and_10_out, and_11_out, and_12_out, and_13_out);
  or or_4 (S1, and_14_out, and_15_out, and_16_out, and_17_out);
  or or_5 (S0, and_18_out, and_19_out, and_20_out, and_21_out);
endmodule

module contador_amarillo (
  input  Q1,
  input  Q0,
  output FF1,
  output FF0
);

  wire and_1_out, and_2_out, not_1_out, not_2_out;

  not not_1 (not_1_out, Q1);
  not not_2 (not_2_out, Q0);
  not not_3 (FF0, Q0);
  and and_1 (and_1_out, Q1, Q0);
  and and_2 (and_2_out, not_1_out, not_2_out);
  or or_1 (FF1, and_1_out, and_2_out);
endmodule

module switch (
  input  A3,
  input  B4,
  input  A2,
  input  B0,
  input  A1,
  input  B1,
  input  A0,
  input  B2,
  input  B3,
  output S2,
  output S0,
  output S1
);

  wire not_1_out, rojo_s;

  stop_verde verde (.B3(A3), .B2(A2), .B1(A1), .B0(A0), .S(S1));
  not not_1 (not_1_out, S1);
  or or_1 (S0, not_1_out, rojo_s);
  stop_rojo rojo (.B3(B3), .B2(B2), .B1(B1), .B0(B0), .B4(B4), .S(rojo_s));
  start_amarillo amarillo (.B5(1'b0), .B4(B4), .B3(B3), .B2(B2), .B1(B1), .B0(B0), .S(S2));

  // Notes on the sheet:
  //   S0: stop verde / S1: stop rojo / S2: start amarillo
endmodule

module stop_verde (
  input  B3,
  input  B2,
  input  B1,
  input  B0,
  output S
);

  comparador_cero comparador_cero_1 (
    .A1(1'b0), .A3(1'b0), .A5(1'b0), .A0(1'b0), .A2(1'b0), .A4(1'b0), .B1(B1), .B3(B3), .B5(1'b0), .B0(B0),
    .B2(B2), .B4(1'b0), .S(S));

  // Notes on the sheet:
  //   A5 A4 A3 A2 A1 A0
  //   Compara si ambos numeros (A y B) son cero
  //   B5 B4
endmodule

module stop_rojo (
  input  B3,
  input  B2,
  input  B1,
  input  B0,
  input  B4,
  output S
);

  comparador_cero comparador_cero_1 (
    .A1(1'b0), .A3(1'b0), .A5(1'b0), .A0(1'b0), .A2(1'b0), .A4(1'b0), .B1(B1), .B3(B3), .B5(1'b0), .B0(B0),
    .B2(B2), .B4(B4), .S(S));

  // Notes on the sheet:
  //   Compara si ambos numeros (A y B) son cero
  //   A5 A4 A3 A2 A1 A0
  //   B5
endmodule

module start_amarillo (
  input  B5,
  input  B4,
  input  B3,
  input  B2,
  input  B1,
  input  B0,
  output S
);

  wire comparador_16_bits_1_a___b, comparador_16_bits_1_a_b;

  comparador_16_bits comparador_16_bits_1 (
    .A5(1'b0), .A4(1'b0), .A3(1'b0), .A2(1'b0), .A1(1'b1), .A0(1'b1), .B5(B5), .B4(B4), .B3(B3), .B2(B2),
    .B1(B1), .B0(B0), .A_B(comparador_16_bits_1_a_b), .A___B(comparador_16_bits_1_a___b));  // open: A___B_2
  or or_1 (S, comparador_16_bits_1_a_b, comparador_16_bits_1_a___b);

  // Notes on the sheet:
  //   Se activa si el numero B es igual o menor a tres
endmodule

// 16 bits
module comparador_16_bits (
  input  A5,
  input  A4,
  input  A3,
  input  A2,
  input  A1,
  input  A0,
  input  B5,
  input  B4,
  input  B3,
  input  B2,
  input  B1,
  input  B0,
  output A___B,
  output A___B_2,
  output A_B
);

  wire comparador_8_bits_1_a___b, comparador_8_bits_1_a___b_2, comparador_8_bits_1_a_b,
       comparador_8_bits_2_a___b, comparador_8_bits_2_a___b_2, comparador_8_bits_2_a_b;

  comparador_8_bits comparador_8_bits_1 (
    .A1(A1), .A3(A3), .A0(A0), .A2(A2), .B1(B1), .B3(B3), .B0(B0), .B2(B2), .A_B(comparador_8_bits_1_a_b),
    .A___B(comparador_8_bits_1_a___b), .A___B_2(comparador_8_bits_1_a___b_2));
  and and_1 (A_B, comparador_8_bits_1_a_b, comparador_8_bits_2_a_b);
  comparador_8_bits comparador_8_bits_2 (
    .A1(A5), .A3(1'b0), .A0(A4), .A2(1'b0), .B1(B5), .B3(1'b0), .B0(B4), .B2(1'b0),
    .A_B(comparador_8_bits_2_a_b), .A___B(comparador_8_bits_2_a___b), .A___B_2(comparador_8_bits_2_a___b_2));
  comparador_4_bits comparador_4_bits_1 (
    .A1(comparador_8_bits_2_a___b), .A0(comparador_8_bits_1_a___b), .B1(comparador_8_bits_2_a___b_2),
    .B0(comparador_8_bits_1_a___b_2), .A_B(A___B), .A_B_2(A___B_2));  // open: A_B_3

  // Notes on the sheet:
  //   Comparador de 16 bits
endmodule

// 8 BITS
module comparador_8_bits (
  input  A1,
  input  A3,
  input  A0,
  input  A2,
  input  B1,
  input  B3,
  input  B0,
  input  B2,
  output A___B,
  output A___B_2,
  output A_B
);

  wire comparador_4_bits_1_a_b, comparador_4_bits_1_a_b_2, comparador_4_bits_1_a_b_3,
       comparador_4_bits_2_a_b, comparador_4_bits_2_a_b_2, comparador_4_bits_2_a_b_3;

  comparador_4_bits comparador_4_bits_1 (
    .A1(A1), .A0(A0), .B1(B1), .B0(B0), .A_B(comparador_4_bits_1_a_b), .A_B_2(comparador_4_bits_1_a_b_2),
    .A_B_3(comparador_4_bits_1_a_b_3));
  and and_1 (A_B, comparador_4_bits_1_a_b_3, comparador_4_bits_2_a_b_3);
  comparador_4_bits comparador_4_bits_2 (
    .A1(A3), .A0(A2), .B1(B3), .B0(B2), .A_B(comparador_4_bits_2_a_b), .A_B_2(comparador_4_bits_2_a_b_2),
    .A_B_3(comparador_4_bits_2_a_b_3));
  comparador_4_bits comparador_4_bits_3 (
    .A1(comparador_4_bits_2_a_b), .A0(comparador_4_bits_1_a_b), .B1(comparador_4_bits_2_a_b_2),
    .B0(comparador_4_bits_1_a_b_2), .A_B(A___B), .A_B_2(A___B_2));  // open: A_B_3

  // Notes on the sheet:
  //   Comparador de 8 bits
endmodule

// 4 bits
module comparador_4_bits (
  input  A1,
  input  A0,
  input  B1,
  input  B0,
  output A_B,
  output A_B_2,
  output A_B_3
);

  wire and_1_out, and_2_out, and_3_out, and_4_out, and_5_out, and_6_out, not_1_out, not_2_out, not_3_out,
       not_4_out, not_5_out, not_6_out, not_7_out, not_8_out, xnor_1_out, xnor_2_out;

  not not_1 (not_1_out, B1);
  not not_2 (not_2_out, B1);
  not not_3 (not_3_out, B0);
  not not_4 (not_4_out, B0);
  not not_5 (not_5_out, A1);
  not not_6 (not_6_out, A0);
  not not_7 (not_7_out, A1);
  not not_8 (not_8_out, A0);
  xnor xnor_1 (xnor_1_out, A1, B1);
  xnor xnor_2 (xnor_2_out, A0, B0);
  and and_1 (and_1_out, A1, not_1_out);
  and and_2 (and_2_out, A0, not_2_out, not_3_out);
  and and_3 (and_3_out, A1, A0, not_4_out);
  and and_4 (and_4_out, not_5_out, B1);
  and and_5 (and_5_out, not_6_out, B1, B0);
  and and_6 (and_6_out, not_7_out, not_8_out, B0);
  and and_7 (A_B_3, xnor_1_out, xnor_2_out);
  or or_1 (A_B, and_1_out, and_2_out, and_3_out);
  or or_2 (A_B_2, and_4_out, and_5_out, and_6_out);

  // Notes on the sheet:
  //   Comparador de 4 bits
endmodule

module comparador_cero (
  input  A1,
  input  A3,
  input  A5,
  input  A0,
  input  A2,
  input  A4,
  input  B1,
  input  B3,
  input  B5,
  input  B0,
  input  B2,
  input  B4,
  output S
);

  wire and_1_out, and_3_out, and_4_out, not_1_out, not_2_out, not_3_out, not_4_out, not_5_out, not_6_out,
       not_7_out, not_8_out, not_9_out, not_10_out, not_11_out, not_12_out;

  not not_1 (not_1_out, A1);
  not not_2 (not_2_out, A0);
  not not_3 (not_3_out, B1);
  not not_4 (not_4_out, B0);
  and and_1 (and_1_out, not_1_out, not_2_out, not_3_out, not_4_out);
  and and_2 (S, and_1_out, and_3_out, and_4_out);
  not not_5 (not_5_out, A3);
  not not_6 (not_6_out, A2);
  not not_7 (not_7_out, B3);
  not not_8 (not_8_out, B2);
  and and_3 (and_3_out, not_5_out, not_6_out, not_7_out, not_8_out);
  not not_9 (not_9_out, A5);
  not not_10 (not_10_out, A4);
  not not_11 (not_11_out, B5);
  not not_12 (not_12_out, B4);
  and and_4 (and_4_out, not_9_out, not_10_out, not_11_out, not_12_out);

  // Notes on the sheet:
  //   Compara si ambos numeros (A y B) son cero
endmodule

module bcd (
  input  B4,
  input  B3,
  input  B2,
  input  B1,
  input  B0,
  output S7,
  output S6,
  output S5,
  output S4,
  output S3,
  output S2,
  output S1,
  output S0
);

  wire and_1_out, and_2_out, and_3_out, and_4_out, and_5_out, and_6_out, and_7_out, and_8_out, and_9_out,
       and_10_out, and_11_out, and_12_out, and_13_out, and_14_out, not_1_out, not_2_out, not_3_out,
       not_4_out, not_5_out, not_6_out, not_7_out, not_8_out, not_9_out, not_10_out, not_11_out, not_12_out,
       not_13_out, not_14_out, not_15_out, not_16_out, not_17_out, not_18_out;

  and and_1 (and_1_out, B4, B2);
  and and_2 (and_2_out, B4, B3);
  not not_1 (not_1_out, B3);
  not not_2 (not_2_out, B2);
  not not_3 (not_3_out, B2);
  not not_4 (not_4_out, B4);
  not not_5 (not_5_out, B2);
  not not_6 (not_6_out, B1);
  not not_7 (not_7_out, B4);
  not not_8 (not_8_out, B3);
  not not_9 (not_9_out, B4);
  not not_10 (not_10_out, B2);
  not not_11 (not_11_out, B1);
  not not_12 (not_12_out, B4);
  not not_13 (not_13_out, B3);
  not not_14 (not_14_out, B3);
  not not_15 (not_15_out, B1);
  not not_16 (not_16_out, B3);
  not not_17 (not_17_out, B2);
  not not_18 (not_18_out, B1);
  or or_1 (S5, and_1_out, and_2_out);
  and and_3 (and_3_out, B3, B1);
  and and_4 (and_4_out, B3, B2);
  and and_5 (and_5_out, B4, not_1_out, not_2_out);
  and and_6 (and_6_out, B4, not_3_out, B1);
  and and_7 (and_7_out, not_4_out, B3, not_5_out, not_6_out);
  and and_8 (and_8_out, not_7_out, not_8_out, B2);
  and and_9 (and_9_out, not_9_out, B2, B1);
  and and_10 (and_10_out, B4, not_10_out, not_11_out);
  and and_11 (and_11_out, not_12_out, not_13_out, B1);
  and and_12 (and_12_out, not_14_out, B2, B1);
  and and_13 (and_13_out, B3, B2, not_15_out);
  and and_14 (and_14_out, B4, not_16_out, not_17_out, not_18_out);
  or or_2 (S4, and_3_out, and_4_out, and_5_out);
  or or_3 (S3, and_6_out, and_7_out);
  or or_4 (S2, and_8_out, and_9_out, and_10_out);
  or or_5 (S1, and_11_out, and_12_out, and_13_out, and_14_out);

  assign S0 = B0;
  assign S6 = 1'b0;
  assign S7 = 1'b0;

  // Notes on the sheet:
  //   Binario a decimal
endmodule

module decoder (
  input  B3,
  input  B2,
  input  B1,
  input  B0,
  output a,
  output b,
  output c,
  output d,
  output e,
  output f,
  output g
);

  wire and_1_out, and_2_out, and_3_out, and_4_out, and_5_out, and_6_out, and_7_out, and_8_out, and_9_out,
       and_10_out, and_11_out, and_12_out, and_13_out, and_14_out, and_15_out, and_16_out, not_1_out,
       not_2_out, not_3_out, not_4_out, not_5_out, not_6_out, not_7_out, not_8_out, not_9_out, not_10_out,
       not_11_out, not_12_out, not_13_out, not_14_out, not_15_out, not_16_out, not_17_out, not_18_out,
       not_19_out, not_20_out, not_21_out;

  not not_1 (not_1_out, B2);
  and and_1 (and_1_out, not_1_out, not_2_out);
  not not_2 (not_2_out, B0);
  and and_2 (and_2_out, B2, B0);
  not not_3 (not_3_out, B2);
  not not_4 (not_4_out, B1);
  and and_3 (and_3_out, not_4_out, not_5_out);
  not not_5 (not_5_out, B0);
  and and_4 (and_4_out, B1, B0);
  not not_6 (not_6_out, B1);
  or or_1 (c, not_6_out, B0, B2);
  not not_7 (not_7_out, B2);
  and and_5 (and_5_out, not_7_out, not_8_out);
  not not_8 (not_8_out, B0);
  not not_9 (not_9_out, B2);
  and and_6 (and_6_out, not_9_out, B1);
  and and_7 (and_7_out, B1, not_10_out);
  not not_10 (not_10_out, B0);
  and and_8 (and_8_out, B2, not_11_out, B0);
  not not_11 (not_11_out, B1);
  not not_12 (not_12_out, B2);
  and and_9 (and_9_out, not_12_out, not_13_out);
  not not_13 (not_13_out, B0);
  and and_10 (and_10_out, B1, not_14_out);
  not not_14 (not_14_out, B0);
  not not_15 (not_15_out, B1);
  and and_11 (and_11_out, not_15_out, not_16_out);
  not not_16 (not_16_out, B0);
  and and_12 (and_12_out, B2, not_17_out);
  not not_17 (not_17_out, B1);
  and and_13 (and_13_out, B2, not_18_out);
  not not_18 (not_18_out, B0);
  not not_19 (not_19_out, B2);
  and and_14 (and_14_out, not_19_out, B1);
  and and_15 (and_15_out, B2, not_20_out);
  not not_20 (not_20_out, B1);
  and and_16 (and_16_out, B2, not_21_out);
  not not_21 (not_21_out, B0);
  or or_2 (a, and_1_out, B1, and_2_out, B3);
  or or_3 (b, not_3_out, and_3_out, and_4_out);
  or or_4 (d, and_5_out, and_6_out, and_7_out, and_8_out);
  or or_5 (e, and_9_out, and_10_out);
  or or_6 (f, and_11_out, and_12_out, and_13_out, B3);
  or or_7 (g, and_14_out, and_15_out, and_16_out, B3);

  // Notes on the sheet:
  //   decoder de 4 bits a display de 7 segmentos
endmodule
